// Digital circuit or.dig as structural Verilog
module \or  (
  input  a,
  input  b,
  output out
);

  wire not_1_out, not_2_out;

  not not_1 (not_1_out, a);
  not not_2 (not_2_out, b);
  nand nand_1 (out, not_1_out, not_2_out);
endmodule
